// Logisim project LOTP_8-Bit-CPU-V4-7400.circ as structural Verilog: 2 circuits, main circuit main
module main (
  input  in_1,
  input  in_2,
  input  [7:0] in_3,
  input  [7:0] in_4
);

  // Probe on in_3
  DIP_74245 dip_74245_1 (
    .DIR(in_1), .B1_2(in_4[0]), .B1(in_4[0]), .A1(in_3[0]), .A1_2(in_3[0]), .B2_2(in_4[1]), .B2(in_4[1]),
    .A2(in_3[1]), .A2_2(in_3[1]), .B3_2(in_4[2]), .B3(in_4[2]), .A3(in_3[2]), .A3_2(in_3[2]), .B4_2(in_4[3]),
    .B4(in_4[3]), .A4(in_3[3]), .A4_2(in_3[3]), .B5_2(in_4[4]), .B5(in_4[4]), .B6_2(in_4[5]), .B6(in_4[5]),
    .A5(in_3[4]), .A5_2(in_3[4]), .A6(in_3[5]), .A6_2(in_3[5]), .B7_2(in_4[6]), .B7(in_4[6]), .B8_2(in_4[7]),
    .B8(in_4[7]), .A7(in_3[6]), .A7_2(in_3[6]), .A8(in_3[7]), .A8_2(in_3[7]), .EN_prime(in_2));
  // Probe on in_4
endmodule

module DIP_74245 (
  input  EN_prime,
  input  B1,
  input  B2,
  input  B3,
  input  B4,
  input  B5,
  input  B6,
  input  B7,
  input  B8,
  input  A1,
  input  A2,
  input  A3,
  input  A4,
  input  A5,
  input  A6,
  input  A7,
  input  A8,
  input  DIR,
  output B1_2,
  output B2_2,
  output B3_2,
  output B4_2,
  output B5_2,
  output B6_2,
  output B7_2,
  output B8_2,
  output A1_2,
  output A2_2,
  output A3_2,
  output A4_2,
  output A5_2,
  output A6_2,
  output A7_2,
  output A8_2
);

  wire and_1_out, and_2_out, not_1_out, not_2_out, not_3_out;

  not not_1 (not_1_out, DIR);
  not not_2 (not_2_out, EN_prime);
  and and_1 (and_1_out, not_1_out, not_2_out);
  assign B1_2 = and_2_out ? A1 : 1'bz;  // Controlled_Buffer controlled_buffer_1
  and and_2 (and_2_out, DIR, not_3_out);
  not not_3 (not_3_out, EN_prime);
  assign A1_2 = and_1_out ? B1 : 1'bz;  // Controlled_Buffer controlled_buffer_2
  assign A2_2 = and_1_out ? B2 : 1'bz;  // Controlled_Buffer controlled_buffer_3
  assign B3_2 = and_2_out ? A3 : 1'bz;  // Controlled_Buffer controlled_buffer_4
  assign B2_2 = and_2_out ? A2 : 1'bz;  // Controlled_Buffer controlled_buffer_5
  assign A3_2 = and_1_out ? B3 : 1'bz;  // Controlled_Buffer controlled_buffer_6
  assign A4_2 = and_1_out ? B4 : 1'bz;  // Controlled_Buffer controlled_buffer_7
  assign B4_2 = and_2_out ? A4 : 1'bz;  // Controlled_Buffer controlled_buffer_8
  assign B5_2 = and_2_out ? A5 : 1'bz;  // Controlled_Buffer controlled_buffer_9
  assign A5_2 = and_1_out ? B5 : 1'bz;  // Controlled_Buffer controlled_buffer_10
  assign A6_2 = and_1_out ? B6 : 1'bz;  // Controlled_Buffer controlled_buffer_11
  assign B6_2 = and_2_out ? A6 : 1'bz;  // Controlled_Buffer controlled_buffer_12
  assign B7_2 = and_2_out ? A7 : 1'bz;  // Controlled_Buffer controlled_buffer_13
  assign A7_2 = and_1_out ? B7 : 1'bz;  // Controlled_Buffer controlled_buffer_14
  assign A8_2 = and_1_out ? B8 : 1'bz;  // Controlled_Buffer controlled_buffer_15
  assign B8_2 = and_2_out ? A8 : 1'bz;  // Controlled_Buffer controlled_buffer_16
endmodule
